# Fritzing sketch ProtoPhoton (saved by Fritzing 0.9.2b)
circuit board: 7.8cm x 5.8cm
perfboards: 1

parts:
  J1 = Screw terminal - 2 pins [package=THT]
  Photon = Photon
  Ultrasound_3 = Header 4 [package=molex-1x4_lock]
  Ultrasound_0 = Header 4 [package=molex-1x4_lock]
  Ultrasound_1 = Header 4 [package=molex-1x4_lock]
  Ultrasound_5 = Header 4 [package=molex-1x4_lock]
  Ultrasound_4 = Header 4 [package=molex-1x4_lock]
  Ultrasound_2 = Header 4 [package=molex-1x4_lock]

nets:
  N1: J1.pin1, Photon.GND, Ultrasound_3.2, Ultrasound_0.2, Ultrasound_1.2, Ultrasound_5.2, Ultrasound_4.2, Ultrasound_2.2
  N2: J1.pin2, Photon.VIN
  N3: Photon.A0, Ultrasound_0.3
  N4: Photon.A1, Ultrasound_1.3
  N5: Photon.A2, Ultrasound_2.3
  N6: Photon.A3, Ultrasound_3.3
  N7: Photon.A4, Ultrasound_4.3
  N8: Photon.A5, Ultrasound_5.3
  N9: Photon.D0, Ultrasound_0.4
  N10: Photon.D1, Ultrasound_1.4
  N11: Photon.D2, Ultrasound_2.4
  N12: Photon.D3, Ultrasound_3.4
  N13: Photon.D4, Ultrasound_4.4
  N14: Photon.D5, Ultrasound_5.4
  N15: Photon.3V3, Ultrasound_3.1, Ultrasound_0.1, Ultrasound_1.1, Ultrasound_5.1, Ultrasound_4.1, Ultrasound_2.1
